# Fritzing sketch SawVCO (saved by Fritzing 0.9.4)
breadboards: 2
perfboards: 1

parts:
  IC1 = Dual Op-Amp [package=dip08]
  R1 = Resistor [tolerance=±5% resistance=47k package=THT]
  R2 = Resistor [tolerance=±5% resistance=33k package=THT]
  C1 = Ceramic Capacitor [capacitance=100nF package="100 mil [THT, multilayer]"]
  C2 = Ceramic Capacitor [capacitance=100nF package="100 mil [THT, multilayer]"]
  IC2 = Dual Op-Amp [package=dip08]
  C3 = Ceramic Capacitor [capacitance=100nF package="100 mil [THT, multilayer]"]
  C4 = Ceramic Capacitor [capacitance=100nF package="100 mil [THT, multilayer]"]
  C5 = Electrolytic Capacitor [capacitance=1µF package="100 mil [THT, electrolytic]"]
  R3 = Resistor [tolerance=±5% resistance=100k package=THT]
  J1 = female pin header, 3 pins [form="♀ (female)"]
  J2 = female pin header, 3 pins [form="♀ (female)"]
  J3 = female pin header, 2 pins [form="♀ (female)"]
  J4 = female pin header, 2 pins [form="♀ (female)"]
  R4 = Resistor [tolerance=±5% resistance=100k package=THT]
  C6 = Film/Foil Capacitor [capacitance=100nF voltage=35V package="5mm [THT, pp]"]
  J5 = female pin header, 2 pins [form="♀ (female)"]
  C7 = Film/Foil Capacitor [capacitance=100nF voltage=35V package="5mm [THT, pp]"]
  R5 = TRIMPOT [package=trimpot_pth_s3_lock]
  Q1 = PNP-Transistor [package="TO92 [THT]"]
  R6 = Resistor [tolerance=±5% resistance=150 package=THT]
  R7 = Resistor [tolerance=±5% resistance=680 package=THT]
  C8 = Ceramic Capacitor [capacitance=100nF package="100 mil [THT, multilayer]"]
  R8 = Resistor [tolerance=±5% resistance=10k package=THT]
  R9 = Resistor [tolerance=±5% resistance=22k package=THT]
  J6 = female pin header, 2 pins [form="♀ (female)"]
  R11 = Resistor [tolerance=±5% resistance=100k package=THT]
  R12 = Resistor [tolerance=±5% resistance=100k package=THT]
  R13 = Resistor [tolerance=±5% resistance=120k package=THT]
  R14 = Resistor [tolerance=±5% resistance=100k package=THT]
  R15 = Resistor [tolerance=±5% resistance=2.2k package=THT]
  J7 = female pin header, 2 pins [form="♀ (female)"]
  R16 = Rotary Potentiometer (Small) [maximum_resistance=100kΩ package=THT]
  J8 = female pin header, 2 pins [form="♀ (female)"]  # not connected
  C9 = Electrolytic Capacitor [capacitance=1µF package="100 mil [THT, electrolytic]"]
  C10 = Electrolytic Capacitor [capacitance=1µF package="100 mil [THT, electrolytic]"]

nets:
  N1: IC1.A_OUT, IC1.A_-IN, C5.+, R3.Pin_0, C7.-, Q1.E, R6.Pin_0, R11.Pin_0, R14.Pin_0
  N2: IC1.A_+IN, R1.Pin_1, R2.Pin_1
  N3: IC1.A_V-, C2.0, IC2.A_V-, C4.0, J1.pin3, C10.-
  N4: IC1.B_+IN, R2.Pin_0, C1.1, C2.1, C3.1, C4.1, C5.-, J1.pin2, J3.pin2, J4.pin2, J5.pin2, R8.Pin_0, J6.pin2, J7.pin2, C9.-, C10.+
  N5: IC1.B_-IN, IC1.B_OUT
  N6: IC1.A_V+, R1.Pin_0, C1.0, IC2.A_V+, C3.0, J1.pin1, C9.+
  N7: IC2.A_OUT, R12.Pin_1, R13.Pin_0, R15.Pin_0
  N8: IC2.A_-IN, R13.Pin_1, R14.Pin_1
  N9: IC2.A_+IN, J3.pin1, R5.CW
  N10: IC2.B_+IN, C8.1, R11.Pin_1, R12.Pin_0
  N11: IC2.B_-IN, R8.Pin_1, R9.Pin_0
  N12: IC2.B_OUT, R7.Pin_1, C8.0
  N13: R3.Pin_1, J4.pin1, R4.Pin_1
  N14: J2.pin1, R16.leg2
  N15: J2.pin2, R16.wiper
  N16: J2.pin3, R16.leg1
  N17: R4.Pin_0, C6.-
  N18: C6.+, J5.pin1
  N19: C7.+, R5.CCW, R5.WIPER, Q1.B
  N20: Q1.C, R6.Pin_1, R7.Pin_0
  N21: R9.Pin_1, J6.pin1
  N22: R15.Pin_1, J7.pin1

notes:
  -12V
  GND
  GND
  +12V
  GND
  +5V
  -12V G -12V
  Antilog_NPNO 改
  Linier FM
  2SA1015 E / C / B
  Sync In
  Saw Out
  CV Oct/V
  Frequency
  I_Sink
  I_Ref
